# Fritzing sketch Tejibot_Wheels (saved by Fritzing 0.9.3b)
breadboards: 1

parts:
  S1 = H-Bridge with L298N
  Part1 = Bluetooth HC-05 Macho
  Part2 = Arduino Uno (Rev3)
  BAT1 = BC9VPC [package=bc9vpc]
  S2 = Toggle Switch [package=THT]
  IC1 = Voltage Regulator [package=to220-igo]
  M2 = DC Motor
  M3 = DC Motor
  BAT2 = BC9VPC [package=bc9vpc]

nets:
  N1: S1.12V, BAT2.V+
  N2: S1.GND, BAT2.V-
  5V: S1.5V, Part2.5V, IC1.OUT
  N3: S1.ENA, Part2.D6_PWM
  N4: S1.IN1, Part2.D13/SCK
  N5: S1.IN2, Part2.D12/MISO
  N6: S1.IN3, Part2.D11_PWM/MOSI
  N7: S1.IN4, Part2.D10_PWM/SS
  N8: S1.ENB, Part2.D5_PWM
  N9: S1.M1-01, M2.pin_2
  N10: S1.M1-02, M2.pin_1
  N11: S1.M2-01, M3.pin_1
  N12: S1.M2-02, M3.pin_2
  N13: Part1.TXD, Part2.D0/RX
  N14: Part1.RXD, Part2.D1/TX
  VCC: Part1.VCC, Part2.3V3
  GND: Part1.GND, Part2.GND, BAT1.V-, IC1.IN
  N15: BAT1.V+, S2.COM
  N16: S2.L2, IC1.GND

custom parts:
  H-Bridge with L298N: h-bridge

// code stored in the sketch: teiji_bot_code_for_bluetooth_control_V1.ino
char t;
 
void setup() {
    
pinMode(13,OUTPUT);   //in1 neg motors forward
pinMode(12,OUTPUT);   //in2 pos motors reverse
pinMode(11,OUTPUT);   //right motors forward
pinMode(10,OUTPUT);   //right motors reverse
pinMode(6, OUTPUT);
pinMode(3, OUTPUT);

Serial.begin(9600);

}
 
void loop() {
if(Serial.available()){
  t = Serial.read();
  Serial.println(t);
}
 
if(t == 'F'){            //move forward(all motors rotate in forward direction)
 digitalWrite(12,LOW);
  digitalWrite(13,HIGH);
  analogWrite(6, 255);
analogWrite(3, 85);
}
 
else if(t == 'B'){      //move reverse (all motors rotate in reverse direction)
  
  
  digitalWrite(12,HIGH);
  digitalWrite(13,LOW);
  analogWrite(6, 255);
}
 
else if(t == 'L'){      //turn right (left side motors rotate in forward direction, right side motors doesn't rotate)
  digitalWrite(11,HIGH);
	analogWrite(3, 64);
// range for left motor is 59-80

}
 
else if(t == 'R'){      //turn left (right side motors rotate in forward direction, left side motors doesn't rotate)
  digitalWrite(13,HIGH);
analogWrite(3, 95);
// range for left motor is 90-110
}

else if(t == 'W'){    //turn led on or off)
  digitalWrite(9,HIGH);
}
else if(t == 'w'){
  digitalWrite(9,LOW);
}
 
else if(t == 'S'){      //STOP (all motors stop)
  digitalWrite(13,LOW);
  digitalWrite(12,LOW);
  digitalWrite(11,LOW);
  digitalWrite(10,LOW);
}
}
